// Logisim project BCDtoSeg.circ as structural Verilog: 3 circuits, main circuit BCDtoSeg
module BCDtoSeg (
  input  [3:0] in_1,
  input  in_2,
  output [3:0] out_3,
  output [3:0] out_4
);

  wire and_1_out, and_2_out, and_3_out, and_4_out, and_5_out, and_6_out, and_7_out, and_8_out, and_9_out,
       and_10_out, and_11_out, and_12_out, and_13_out, and_14_out, and_15_out, and_16_out, and_17_out,
       not_1_out, not_2_out, not_3_out, not_4_out;

  not not_1 (not_1_out, in_1[0]);
  not not_2 (not_2_out, in_1[1]);
  not not_3 (not_3_out, in_1[2]);
  not not_4 (not_4_out, in_1[3]);
  and and_1 (and_1_out, in_1[1], not_3_out);
  and and_2 (and_2_out, in_1[2], not_2_out);
  and and_3 (and_3_out, in_1[3], not_3_out, not_2_out);
  and and_4 (and_4_out, not_4_out, in_1[2], in_1[1], not_1_out);
  and and_5 (and_5_out, not_2_out, not_3_out, not_4_out, not_1_out);
  and and_6 (and_6_out, in_1[2], in_1[1], not_1_out);
  and and_7 (and_7_out, not_4_out, not_3_out, not_2_out);
  and and_8 (and_8_out, not_4_out, not_3_out, in_1[1]);
  and and_9 (and_9_out, in_1[3], not_3_out, not_2_out, not_1_out);
  and and_10 (and_10_out, not_4_out, not_3_out, in_1[1], not_1_out);
  and and_11 (and_11_out, not_4_out, in_1[2], not_2_out, in_1[0]);
  and and_12 (and_12_out, not_4_out, in_1[2]);
  and and_13 (and_13_out, not_4_out, not_3_out, in_1[1], in_1[0]);
  and and_14 (and_14_out, not_4_out, in_1[2], not_2_out, not_1_out);
  and and_15 (and_15_out, not_4_out, not_3_out);
  and and_16 (and_16_out, not_4_out, in_1[2], in_1[1]);
  and and_17 (and_17_out, not_4_out, in_1[2], in_1[1], in_1[0]);
  or or_1 (out_3[3], and_1_out, and_2_out, and_3_out, and_4_out);
  or or_2 (out_3[2], and_2_out, and_3_out, and_6_out, and_5_out);
  or or_3 (out_3[1], and_8_out, and_4_out, and_11_out, and_5_out, and_3_out, and_16_out);
  or or_4 (out_3[0], and_14_out, and_9_out, and_3_out, and_15_out, and_5_out, and_17_out);
  or or_5 (out_4[3], and_10_out, and_4_out, and_9_out, and_5_out);
  or or_6 (out_4[2], and_8_out, and_11_out, and_4_out, and_3_out, and_5_out);
  or or_7 (out_4[1], and_7_out, and_12_out, and_3_out, and_13_out, and_5_out);

  assign out_4[0] = in_2;
endmodule

module _10_Counter (
  input  in_1,
  output [3:0] out_2,
  output out_3
);

  wire and_1_out, and_2_out, and_3_out, and_4_out, clock_1_out, not_1_out, not_2_out;

  and and_1 (and_1_out, in_1, out_2[0]);
  and and_2 (and_2_out, and_1_out, out_2[1]);
  and and_3 (and_3_out, and_2_out, out_2[2]);
  Clock #(.highDuration(1), .lowDuration(1)) clock_1 (.out(clock_1_out));
  J_K_Flip_Flop j_k_ff_1 (
    .J(in_1), .clk(clock_1_out), .K(in_1), .Q(out_2[0]), .reset(and_4_out));  // open: Qn, preset, en
  J_K_Flip_Flop j_k_ff_2 (
    .J(and_1_out), .clk(clock_1_out), .K(and_1_out), .Q(out_2[1]), .reset(and_4_out));  // open: Qn, preset, en
  J_K_Flip_Flop j_k_ff_3 (
    .J(and_2_out), .clk(clock_1_out), .K(and_2_out), .Q(out_2[2]), .reset(and_4_out));  // open: Qn, preset, en
  J_K_Flip_Flop j_k_ff_4 (
    .J(and_3_out), .clk(clock_1_out), .K(and_3_out), .Q(out_2[3]), .reset(and_4_out));  // open: Qn, preset, en
  not not_1 (not_1_out, out_2[0]);
  and and_4 (and_4_out, not_1_out, out_2[1], not_2_out, out_2[3]);
  not not_2 (not_2_out, out_2[2]);
  and and_5 (out_3, out_2[3], and_3_out);
endmodule

module main (
  input  in_1
);

  wire [3:0] bcdtoseg_1_out_3, bcdtoseg_1_out_4, n10_counter_1_out_2;

  _10_Counter u_10_counter_1 (.in_1(in_1), .out_2(n10_counter_1_out_2));  // open: out_3
  BCDtoSeg bcdtoseg_1 (.in_1(n10_counter_1_out_2), .out_3(bcdtoseg_1_out_3), .out_4(bcdtoseg_1_out_4));  // open: in_2
  _7_Segment_Display u_7_segment_display_1 (
    .g(bcdtoseg_1_out_3[3]), .f(bcdtoseg_1_out_3[2]), .a(bcdtoseg_1_out_3[1]), .b(bcdtoseg_1_out_3[0]),
    .e(bcdtoseg_1_out_4[3]), .d(bcdtoseg_1_out_4[2]), .c(bcdtoseg_1_out_4[1]), .dp(bcdtoseg_1_out_4[0]));
endmodule
